# Fritzing sketch ArduinoLEDSketch (saved by Fritzing 0.9.2b)
breadboards: 1

parts:
  Part1 = Arduino Uno (Rev3) - ICSP
  LED1 = LEDs [package=led10mm]  # not connected
  J1 = Piezo Speaker
  U1 = 74HC595 SMD [package="SO16 [SMD]"]  # not connected
  U2 = 74HC595 SMD [package="SO16 [SMD]"]  # not connected
  S1 = Square Pushbutton  # not connected
  LED2 = LED - 5mm [color="Red (633nm)" package="5 mm [THT]"]  # not connected
  LED3 = LED - 5mm [color="Red (633nm)" package="5 mm [THT]"]  # not connected
  LED4 = LED - 5mm [color="Red (633nm)" package="5 mm [THT]"]  # not connected
  LED5 = LED - 5mm [color="Red (633nm)" package="5 mm [THT]"]  # not connected

nets:
  N1: Part1.D8, J1.pin2
  N2: Part1.GND, J1.pin1
