# Fritzing sketch LED control board (saved by Fritzing 0.9.2b)
circuit board: 10.7223cm x 7.42458cm
breadboards: 1

parts:
  IC1 = Voltage Regulator [package=to220-igo]
  R1 = Resistor [tolerance=±5% resistance=2.2k package="1206 [SMD]"]
  R2 = Resistor [tolerance=±5% resistance=680 package="1206 [SMD]"]
  R3 = Resistor [tolerance=±5% resistance=330 package="1206 [SMD]"]
  Q1 = TRANSISTOR_NPN [package=to-92]
  Q2 = TRANSISTOR_NPN [package=to-92]
  Q3 = TRANSISTOR_NPN [package=to-92]
  R4 = Resistor [tolerance=±5% resistance=330 package="1206 [SMD]"]
  R6 = Resistor [tolerance=±5% resistance=1k package="1206 [SMD]"]
  R7 = Resistor [tolerance=±5% resistance=470 package="1206 [SMD]"]
  R8 = Resistor [tolerance=±5% resistance=330 package="1206 [SMD]"]
  R10 = Resistor [tolerance=±5% resistance=330 package="1206 [SMD]"]
  R12 = Resistor [tolerance=±5% resistance=1k package="1206 [SMD]"]
  R13 = Resistor [tolerance=±5% resistance=470 package="1206 [SMD]"]
  R14 = Resistor [tolerance=±5% resistance=330 package="1206 [SMD]"]
  R16 = Resistor [tolerance=±5% resistance=330 package="1206 [SMD]"]
  R18 = Resistor [tolerance=±5% resistance=1k package="1206 [SMD]"]
  R19 = Resistor [tolerance=±5% resistance=470 package="1206 [SMD]"]
  R20 = Resistor [tolerance=±5% resistance=330 package="1206 [SMD]"]
  J1 = Power Jack [package=power_jack_slot]
  Q4 = TRANSISTOR_NPN [package=to-92]
  R21 = Resistor [tolerance=±5% resistance=330 package="1206 [SMD]"]
  R22 = Resistor [tolerance=±5% resistance=470 package="1206 [SMD]"]
  R23 = Resistor [tolerance=±5% resistance=1k package="1206 [SMD]"]
  R24 = Resistor [tolerance=±5% resistance=330 package="1206 [SMD]"]
  Q5 = TRANSISTOR_NPN [package=to-92]
  R25 = Resistor [tolerance=±5% resistance=330 package="1206 [SMD]"]
  R26 = Resistor [tolerance=±5% resistance=470 package="1206 [SMD]"]
  R27 = Resistor [tolerance=±5% resistance=1k package="1206 [SMD]"]
  R28 = Resistor [tolerance=±5% resistance=330 package="1206 [SMD]"]
  Q6 = TRANSISTOR_NPN [package=to-92]
  Q7 = TRANSISTOR_NPN [package=to-92]
  R29 = Resistor [tolerance=±5% resistance=330 package="1206 [SMD]"]
  R30 = Resistor [tolerance=±5% resistance=330 package="1206 [SMD]"]
  R31 = Resistor [tolerance=±5% resistance=470 package="1206 [SMD]"]
  R32 = Resistor [tolerance=±5% resistance=470 package="1206 [SMD]"]
  R33 = Resistor [tolerance=±5% resistance=1k package="1206 [SMD]"]
  R34 = Resistor [tolerance=±5% resistance=1k package="1206 [SMD]"]
  R35 = Resistor [tolerance=±5% resistance=330 package="1206 [SMD]"]
  R36 = Resistor [tolerance=±5% resistance=330 package="1206 [SMD]"]
  Q8 = TRANSISTOR_NPN [package=to-92]
  R37 = Resistor [tolerance=±5% resistance=330 package="1206 [SMD]"]
  R38 = Resistor [tolerance=±5% resistance=470 package="1206 [SMD]"]
  R39 = Resistor [tolerance=±5% resistance=1k package="1206 [SMD]"]
  R40 = Resistor [tolerance=±5% resistance=330 package="1206 [SMD]"]
  Q9 = TRANSISTOR_NPN [package=to-92]
  Q10 = TRANSISTOR_NPN [package=to-92]
  Q11 = TRANSISTOR_NPN [package=to-92]
  Q12 = TRANSISTOR_NPN [package=to-92]
  Q13 = TRANSISTOR_NPN [package=to-92]
  Q14 = TRANSISTOR_NPN [package=to-92]
  Q15 = TRANSISTOR_NPN [package=to-92]
  Q16 = TRANSISTOR_NPN [package=to-92]
  R41 = Resistor [tolerance=±5% resistance=330 package="1206 [SMD]"]
  R42 = Resistor [tolerance=±5% resistance=470 package="1206 [SMD]"]
  R43 = Resistor [tolerance=±5% resistance=1k package="1206 [SMD]"]
  R44 = Resistor [tolerance=±5% resistance=330 package="1206 [SMD]"]
  R45 = Resistor [tolerance=±5% resistance=330 package="1206 [SMD]"]
  R46 = Resistor [tolerance=±5% resistance=330 package="1206 [SMD]"]
  R47 = Resistor [tolerance=±5% resistance=330 package="1206 [SMD]"]
  R48 = Resistor [tolerance=±5% resistance=330 package="1206 [SMD]"]
  R49 = Resistor [tolerance=±5% resistance=330 package="1206 [SMD]"]
  R50 = Resistor [tolerance=±5% resistance=330 package="1206 [SMD]"]
  R51 = Resistor [tolerance=±5% resistance=470 package="1206 [SMD]"]
  R52 = Resistor [tolerance=±5% resistance=470 package="1206 [SMD]"]
  R53 = Resistor [tolerance=±5% resistance=470 package="1206 [SMD]"]
  R54 = Resistor [tolerance=±5% resistance=470 package="1206 [SMD]"]
  R55 = Resistor [tolerance=±5% resistance=470 package="1206 [SMD]"]
  R56 = Resistor [tolerance=±5% resistance=470 package="1206 [SMD]"]
  R57 = Resistor [tolerance=±5% resistance=1k package="1206 [SMD]"]
  R58 = Resistor [tolerance=±5% resistance=1k package="1206 [SMD]"]
  R59 = Resistor [tolerance=±5% resistance=1k package="1206 [SMD]"]
  R60 = Resistor [tolerance=±5% resistance=1k package="1206 [SMD]"]
  R61 = Resistor [tolerance=±5% resistance=1k package="1206 [SMD]"]
  R62 = Resistor [tolerance=±5% resistance=1k package="1206 [SMD]"]
  R63 = Resistor [tolerance=±5% resistance=330 package="1206 [SMD]"]
  R64 = Resistor [tolerance=±5% resistance=330 package="1206 [SMD]"]
  R65 = Resistor [tolerance=±5% resistance=330 package="1206 [SMD]"]
  R66 = Resistor [tolerance=±5% resistance=330 package="1206 [SMD]"]
  R67 = Resistor [tolerance=±5% resistance=330 package="1206 [SMD]"]
  R68 = Resistor [tolerance=±5% resistance=330 package="1206 [SMD]"]
  R69 = Resistor [tolerance=±5% resistance=330 package="1206 [SMD]"]
  R70 = Resistor [tolerance=±5% resistance=470 package="1206 [SMD]"]
  R71 = Resistor [tolerance=±5% resistance=1k package="1206 [SMD]"]
  R72 = Resistor [tolerance=±5% resistance=330 package="1206 [SMD]"]
  U1 = PCF8574 [package="DIP16 [THT]"]  # not connected
  U2 = PCF8574 [package="DIP16 [THT]"]  # not connected

nets (from the pcb view):
  N1: IC1.GND, R2.Pin_1, R3.Pin_1
  N2: IC1.IN, J1.PWR
  N3: IC1.OUT, R3.Pin_0, R4.Pin_1, R8.Pin_1, R10.Pin_1, R14.Pin_1, R16.Pin_1, R20.Pin_1, R21.Pin_1, R24.Pin_1, R25.Pin_1, R28.Pin_1, R29.Pin_1, R30.Pin_1, R35.Pin_1, R36.Pin_1, R37.Pin_1, R40.Pin_1, R41.Pin_1, R44.Pin_1, R45.Pin_1, R46.Pin_1, R47.Pin_1, R48.Pin_1, R49.Pin_1, R50.Pin_1, R63.Pin_1, R64.Pin_1, R65.Pin_1, R66.Pin_1, R67.Pin_1, R68.Pin_1, R69.Pin_1, R72.Pin_1
  N4: R1.Pin_0, Q1.E, Q2.E, Q3.E, J1.GNDBREAK, Q4.E, Q5.E, Q6.E, Q7.E, Q8.E, Q9.E, Q10.E, Q11.E, Q12.E, Q13.E, Q14.E, Q15.E, Q16.E
  N5: R1.Pin_1, R2.Pin_0
  N6: Q1.B, R6.Pin_1
  N7: Q2.B, R12.Pin_1
  N8: Q3.B, R18.Pin_1
  N9: R6.Pin_0, R7.Pin_1
  N10: R12.Pin_0, R13.Pin_1
  N11: R18.Pin_0, R19.Pin_1
  N12: Q4.B, R23.Pin_1
  N13: R22.Pin_1, R23.Pin_0
  N14: Q5.B, R27.Pin_1
  N15: R26.Pin_1, R27.Pin_0
  N16: Q6.B, R33.Pin_1
  N17: Q7.B, R34.Pin_1
  N18: R31.Pin_1, R33.Pin_0
  N19: R32.Pin_1, R34.Pin_0
  N20: Q8.B, R39.Pin_1
  N21: R38.Pin_1, R39.Pin_0
  N22: Q9.B, R43.Pin_1
  N23: Q10.B, R57.Pin_1
  N24: Q11.B, R59.Pin_1
  N25: Q12.B, R58.Pin_1
  N26: Q13.B, R62.Pin_1
  N27: Q14.B, R61.Pin_1
  N28: Q15.B, R60.Pin_1
  N29: Q16.B, R71.Pin_1
  N30: R42.Pin_1, R43.Pin_0
  N31: R51.Pin_1, R57.Pin_0
  N32: R52.Pin_1, R60.Pin_0
  N33: R53.Pin_1, R58.Pin_0
  N34: R54.Pin_1, R62.Pin_0
  N35: R55.Pin_1, R59.Pin_0
  N36: R56.Pin_1, R61.Pin_0
  N37: R70.Pin_1, R71.Pin_0

notes:
  kmkingsbury
  v1.0
